# Fritzing sketch stripboard (saved by Fritzing 0.9.3b)
stripboards: 3
perfboards: 1

parts:
  IC1 = SELECTOR_MULTIPLEXER [package=dil16]
  J1 = female pin header, 8 pins [form="♀ (female)"]
  J2 = female pin header, 8 pins [form="♀ (female)"]
  IC2 = SELECTOR_MULTIPLEXER [package=dil16]
  J3 = female pin header, 8 pins [form="♀ (female)"]
  J4 = female pin header, 8 pins [form="♀ (female)"]
  IC3 = SELECTOR_MULTIPLEXER [package=dil16]
  J5 = female pin header, 8 pins [form="♀ (female)"]
  J6 = female pin header, 8 pins [form="♀ (female)"]
  R1 = Resistor [tolerance=±5% resistance=220 package=THT]
  R2 = Resistor [tolerance=±5% resistance=220 package=THT]
  R3 = Resistor [tolerance=±5% resistance=220 package=THT]
  R4 = Resistor [tolerance=±5% resistance=220 package=THT]
  R5 = Resistor [tolerance=±5% resistance=220 package=THT]
  R6 = Resistor [tolerance=±5% resistance=220 package=THT]
  R7 = Resistor [tolerance=±5% resistance=220 package=THT]
  R8 = Resistor [tolerance=±5% resistance=220 package=THT]
  R9 = Resistor [tolerance=±5% resistance=220 package=THT]
  R10 = Resistor [tolerance=±5% resistance=220 package=THT]
  R11 = Resistor [tolerance=±5% resistance=220 package=THT]
  R12 = Resistor [tolerance=±5% resistance=220 package=THT]
  R13 = Resistor [tolerance=±5% resistance=220 package=THT]
  R14 = Resistor [tolerance=±5% resistance=220 package=THT]
  R15 = Resistor [tolerance=±5% resistance=220 package=THT]
  R16 = Resistor [tolerance=±5% resistance=220 package=THT]
  R17 = Resistor [tolerance=±5% resistance=220 package=THT]
  R18 = Resistor [tolerance=±5% resistance=220 package=THT]
  R19 = Resistor [tolerance=±5% resistance=220 package=THT]
  R20 = Resistor [tolerance=±5% resistance=220 package=THT]
  R21 = Resistor [tolerance=±5% resistance=220 package=THT]
  J7 = female pin header, 2 pins [form="♀ (female)"]
  J8 = female pin header, 2 pins [form="♀ (female)"]
  J9 = female pin header, 2 pins [form="♀ (female)"]
  J10 = female pin header, 2 pins [form="♀ (female)"]
  J11 = female pin header, 2 pins [form="♀ (female)"]
  J12 = female pin header, 2 pins [form="♀ (female)"]
  J13 = female pin header, 2 pins [form="♀ (female)"]
  J14 = female pin header, 2 pins [form="♀ (female)"]
  J15 = female pin header, 2 pins [form="♀ (female)"]
  J16 = female pin header, 2 pins [form="♀ (female)"]
  J17 = female pin header, 2 pins [form="♀ (female)"]
  J18 = female pin header, 2 pins [form="♀ (female)"]
  J19 = female pin header, 2 pins [form="♀ (female)"]
  J20 = female pin header, 2 pins [form="♀ (female)"]
  J21 = female pin header, 2 pins [form="♀ (female)"]
  J22 = female pin header, 2 pins [form="♀ (female)"]
  J23 = female pin header, 2 pins [form="♀ (female)"]
  J24 = female pin header, 2 pins [form="♀ (female)"]
  J25 = female pin header, 2 pins [form="♀ (female)"]
  J26 = female pin header, 2 pins [form="♀ (female)"]
  R22 = Resistor [tolerance=±5% resistance=220 package=THT]
  R23 = Resistor [tolerance=±5% resistance=220 package=THT]
  R24 = Resistor [tolerance=±5% resistance=220 package=THT]
  R25 = Resistor [tolerance=±5% resistance=220 package=THT]
  R26 = Resistor [tolerance=±5% resistance=220 package=THT]
  R27 = Resistor [tolerance=±5% resistance=220 package=THT]
  R28 = Resistor [tolerance=±5% resistance=220 package=THT]
  R29 = Resistor [tolerance=±5% resistance=220 package=THT]
  R30 = Resistor [tolerance=±5% resistance=220 package=THT]
  R31 = Resistor [tolerance=±5% resistance=220 package=THT]
  R32 = Resistor [tolerance=±5% resistance=220 package=THT]
  R33 = Resistor [tolerance=±5% resistance=220 package=THT]
  R34 = Resistor [tolerance=±5% resistance=220 package=THT]
  R35 = Resistor [tolerance=±5% resistance=220 package=THT]
  R36 = Resistor [tolerance=±5% resistance=220 package=THT]
  R37 = Resistor [tolerance=±5% resistance=220 package=THT]
  R38 = Resistor [tolerance=±5% resistance=220 package=THT]
  R39 = Resistor [tolerance=±5% resistance=220 package=THT]
  R40 = Resistor [tolerance=±5% resistance=220 package=THT]
  R41 = Resistor [tolerance=±5% resistance=220 package=THT]
  R42 = Resistor [tolerance=±5% resistance=220 package=THT]
  IC4 = SELECTOR_MULTIPLEXER [package=dil16]
  J27 = female pin header, 8 pins [form="♀ (female)"]
  J28 = female pin header, 8 pins [form="♀ (female)"]
  IC5 = SELECTOR_MULTIPLEXER [package=dil16]
  J29 = female pin header, 8 pins [form="♀ (female)"]
  J30 = female pin header, 8 pins [form="♀ (female)"]
  IC6 = SELECTOR_MULTIPLEXER [package=dil16]
  J31 = female pin header, 8 pins [form="♀ (female)"]
  J32 = female pin header, 8 pins [form="♀ (female)"]
  J36 = female pin header, 2 pins [form="♀ (female)"]
  J37 = female pin header, 2 pins [form="♀ (female)"]
  J38 = female pin header, 2 pins [form="♀ (female)"]
  J39 = female pin header, 2 pins [form="♀ (female)"]
  J40 = female pin header, 2 pins [form="♀ (female)"]
  J41 = female pin header, 2 pins [form="♀ (female)"]
  J42 = female pin header, 2 pins [form="♀ (female)"]
  J43 = female pin header, 2 pins [form="♀ (female)"]
  J44 = female pin header, 2 pins [form="♀ (female)"]
  J45 = female pin header, 2 pins [form="♀ (female)"]
  J46 = female pin header, 2 pins [form="♀ (female)"]
  J47 = female pin header, 2 pins [form="♀ (female)"]
  J48 = female pin header, 2 pins [form="♀ (female)"]
  J49 = female pin header, 2 pins [form="♀ (female)"]
  J50 = female pin header, 2 pins [form="♀ (female)"]
  J51 = female pin header, 2 pins [form="♀ (female)"]
  J52 = female pin header, 2 pins [form="♀ (female)"]
  J53 = female pin header, 2 pins [form="♀ (female)"]
  J54 = female pin header, 2 pins [form="♀ (female)"]
  J55 = female pin header, 2 pins [form="♀ (female)"]
  J174 = female pin header, 1 pin [form="♀ (female)"]
  J180 = female pin header, 1 pin [form="♀ (female)"]
  J182 = female pin header, 1 pin [form="♀ (female)"]
  J183 = female pin header, 1 pin [form="♀ (female)"]
  J184 = female pin header, 1 pin [form="♀ (female)"]
  J185 = female pin header, 1 pin [form="♀ (female)"]
  J188 = female pin header, 1 pin [form="♀ (female)"]
  J189 = female pin header, 1 pin [form="♀ (female)"]
  J191 = female pin header, 1 pin [form="♀ (female)"]
  J194 = female pin header, 1 pin [form="♀ (female)"]
  J196 = female pin header, 1 pin [form="♀ (female)"]
  J197 = female pin header, 1 pin [form="♀ (female)"]
  J198 = female pin header, 1 pin [form="♀ (female)"]
  J199 = female pin header, 1 pin [form="♀ (female)"]
  J200 = female pin header, 1 pin [form="♀ (female)"]
  J201 = female pin header, 1 pin [form="♀ (female)"]
  R67 = Resistor [tolerance=±5% resistance=220 package=THT]
  R68 = Resistor [tolerance=±5% resistance=220 package=THT]
  R69 = Resistor [tolerance=±5% resistance=220 package=THT]
  R70 = Resistor [tolerance=±5% resistance=220 package=THT]
  R73 = Resistor [tolerance=±5% resistance=220 package=THT]
  R74 = Resistor [tolerance=±5% resistance=220 package=THT]
  R75 = Resistor [tolerance=±5% resistance=220 package=THT]
  R76 = Resistor [tolerance=±5% resistance=220 package=THT]
  R77 = Resistor [tolerance=±5% resistance=220 package=THT]
  R78 = Resistor [tolerance=±5% resistance=220 package=THT]
  R79 = Resistor [tolerance=±5% resistance=220 package=THT]
  R80 = Resistor [tolerance=±5% resistance=220 package=THT]
  R81 = Resistor [tolerance=±5% resistance=220 package=THT]
  R82 = Resistor [tolerance=±5% resistance=220 package=THT]
  R83 = Resistor [tolerance=±5% resistance=220 package=THT]
  R84 = Resistor [tolerance=±5% resistance=220 package=THT]
  R85 = Resistor [tolerance=±5% resistance=220 package=THT]
  R86 = Resistor [tolerance=±5% resistance=220 package=THT]
  J204 = female pin header, 1 pin [form="♀ (female)"]
  J205 = female pin header, 1 pin [form="♀ (female)"]
  R87 = Resistor [tolerance=±5% resistance=220 package=THT]
  R88 = Resistor [tolerance=±5% resistance=220 package=THT]
  J206 = female pin header, 1 pin [form="♀ (female)"]
  J207 = female pin header, 1 pin [form="♀ (female)"]
  R89 = Resistor [tolerance=±5% resistance=220 package=THT]
  R90 = Resistor [tolerance=±5% resistance=220 package=THT]
  R91 = Resistor [tolerance=±5% resistance=220 package=THT]
  R92 = Resistor [tolerance=±5% resistance=220 package=THT]
  R93 = Resistor [tolerance=±5% resistance=220 package=THT]
  R94 = Resistor [tolerance=±5% resistance=220 package=THT]
  R95 = Resistor [tolerance=±5% resistance=220 package=THT]
  R96 = Resistor [tolerance=±5% resistance=220 package=THT]
  R97 = Resistor [tolerance=±5% resistance=220 package=THT]
  R98 = Resistor [tolerance=±5% resistance=220 package=THT]
  R99 = Resistor [tolerance=±5% resistance=220 package=THT]
  R100 = Resistor [tolerance=±5% resistance=220 package=THT]
  R101 = Resistor [tolerance=±5% resistance=220 package=THT]
  R102 = Resistor [tolerance=±5% resistance=220 package=THT]
  R103 = Resistor [tolerance=±5% resistance=220 package=THT]
  R104 = Resistor [tolerance=±5% resistance=220 package=THT]
  R105 = Resistor [tolerance=±5% resistance=220 package=THT]
  R106 = Resistor [tolerance=±5% resistance=220 package=THT]
  R107 = Resistor [tolerance=±5% resistance=220 package=THT]
  R108 = Resistor [tolerance=±5% resistance=220 package=THT]
  R109 = Resistor [tolerance=±5% resistance=220 package=THT]
  R110 = Resistor [tolerance=±5% resistance=220 package=THT]
  J208 = female pin header, 1 pin [form="♀ (female)"]  # not connected
  J209 = female pin header, 1 pin [form="♀ (female)"]  # not connected
  J210 = female pin header, 1 pin [form="♀ (female)"]  # not connected
  J211 = female pin header, 1 pin [form="♀ (female)"]  # not connected
  J212 = female pin header, 1 pin [form="♀ (female)"]  # not connected
  J213 = female pin header, 1 pin [form="♀ (female)"]  # not connected
  J214 = female pin header, 1 pin [form="♀ (female)"]  # not connected
  J215 = female pin header, 1 pin [form="♀ (female)"]  # not connected
  J216 = female pin header, 1 pin [form="♀ (female)"]  # not connected
  J217 = female pin header, 1 pin [form="♀ (female)"]  # not connected
  J218 = female pin header, 1 pin [form="♀ (female)"]  # not connected
  J219 = female pin header, 1 pin [form="♀ (female)"]  # not connected
  J220 = female pin header, 1 pin [form="♀ (female)"]  # not connected
  J221 = female pin header, 1 pin [form="♀ (female)"]  # not connected
  J222 = female pin header, 1 pin [form="♀ (female)"]  # not connected
  J223 = female pin header, 1 pin [form="♀ (female)"]  # not connected
  J224 = female pin header, 1 pin [form="♀ (female)"]  # not connected
  J225 = female pin header, 1 pin [form="♀ (female)"]  # not connected
  J226 = female pin header, 1 pin [form="♀ (female)"]  # not connected
  J227 = female pin header, 1 pin [form="♀ (female)"]  # not connected
  IC7 = SELECTOR_MULTIPLEXER [package=dil16]  # not connected
  J228 = female pin header, 8 pins [form="♀ (female)"]
  J229 = female pin header, 8 pins [form="♀ (female)"]
  IC8 = SELECTOR_MULTIPLEXER [package=dil16]  # not connected
  J231 = female pin header, 8 pins [form="♀ (female)"]
  J232 = female pin header, 8 pins [form="♀ (female)"]
  IC9 = SELECTOR_MULTIPLEXER [package=dil16]  # not connected
  J233 = female pin header, 8 pins [form="♀ (female)"]  # not connected
  J234 = female pin header, 8 pins [form="♀ (female)"]  # not connected
  IC10 = SELECTOR_MULTIPLEXER [package=dil16]  # not connected
  J235 = female pin header, 8 pins [form="♀ (female)"]
  J236 = female pin header, 8 pins [form="♀ (female)"]
  IC11 = SELECTOR_MULTIPLEXER [package=dil16]  # not connected
  IC13 = SELECTOR_MULTIPLEXER [package=dil16]  # not connected
  IC14 = SELECTOR_MULTIPLEXER [package=dil16]  # not connected
  J237 = female pin header, 8 pins [form="♀ (female)"]  # not connected
  J238 = female pin header, 8 pins [form="♀ (female)"]  # not connected
  J240 = female pin header, 8 pins [form="♀ (female)"]  # not connected
  J241 = female pin header, 8 pins [form="♀ (female)"]  # not connected
  J242 = female pin header, 8 pins [form="♀ (female)"]  # not connected
  J243 = female pin header, 8 pins [form="♀ (female)"]
  IC15 = SELECTOR_MULTIPLEXER [package=dil16]  # not connected
  IC16 = SELECTOR_MULTIPLEXER [package=dil16]  # not connected
  IC17 = SELECTOR_MULTIPLEXER [package=dil16]  # not connected
  IC18 = SELECTOR_MULTIPLEXER [package=dil16]  # not connected
  IC19 = SELECTOR_MULTIPLEXER [package=dil16]  # not connected
  IC20 = SELECTOR_MULTIPLEXER [package=dil16]  # not connected
  IC21 = SELECTOR_MULTIPLEXER [package=dil16]  # not connected
  J244 = female pin header, 8 pins [form="♀ (female)"]  # not connected
  J245 = female pin header, 8 pins [form="♀ (female)"]  # not connected
  J246 = female pin header, 8 pins [form="♀ (female)"]  # not connected
  J247 = female pin header, 8 pins [form="♀ (female)"]  # not connected
  J248 = female pin header, 8 pins [form="♀ (female)"]  # not connected
  J249 = female pin header, 8 pins [form="♀ (female)"]  # not connected
  J250 = female pin header, 8 pins [form="♀ (female)"]  # not connected
  J251 = female pin header, 8 pins [form="♀ (female)"]  # not connected
  J252 = female pin header, 8 pins [form="♀ (female)"]  # not connected
  J253 = female pin header, 8 pins [form="♀ (female)"]  # not connected
  J254 = female pin header, 8 pins [form="♀ (female)"]  # not connected
  J255 = female pin header, 8 pins [form="♀ (female)"]  # not connected
  J256 = female pin header, 8 pins [form="♀ (female)"]  # not connected
  J257 = female pin header, 8 pins [form="♀ (female)"]  # not connected
  J258 = female pin header, 1 pin [form="♀ (female)"]
  J259 = female pin header, 1 pin [form="♀ (female)"]
  J260 = female pin header, 1 pin [form="♀ (female)"]
  J261 = female pin header, 1 pin [form="♀ (female)"]
  J262 = female pin header, 1 pin [form="♀ (female)"]
  J263 = female pin header, 1 pin [form="♀ (female)"]
  J264 = female pin header, 1 pin [form="♀ (female)"]
  J265 = female pin header, 1 pin [form="♀ (female)"]
  J266 = female pin header, 1 pin [form="♀ (female)"]
  J267 = female pin header, 1 pin [form="♀ (female)"]
  J268 = female pin header, 1 pin [form="♀ (female)"]
  J269 = female pin header, 1 pin [form="♀ (female)"]
  J270 = female pin header, 1 pin [form="♀ (female)"]
  J271 = female pin header, 1 pin [form="♀ (female)"]
  J272 = female pin header, 1 pin [form="♀ (female)"]
  J273 = female pin header, 1 pin [form="♀ (female)"]
  J274 = female pin header, 1 pin [form="♀ (female)"]
  J275 = female pin header, 1 pin [form="♀ (female)"]
  J276 = female pin header, 1 pin [form="♀ (female)"]
  J277 = female pin header, 1 pin [form="♀ (female)"]
  J278 = female pin header, 1 pin [form="♀ (female)"]  # not connected
  J279 = female pin header, 1 pin [form="♀ (female)"]  # not connected
  J280 = female pin header, 1 pin [form="♀ (female)"]  # not connected
  J281 = female pin header, 1 pin [form="♀ (female)"]  # not connected
  J282 = female pin header, 1 pin [form="♀ (female)"]  # not connected
  J283 = female pin header, 1 pin [form="♀ (female)"]  # not connected
  J284 = female pin header, 1 pin [form="♀ (female)"]
  J285 = female pin header, 1 pin [form="♀ (female)"]
  J286 = female pin header, 1 pin [form="♀ (female)"]
  J288 = female pin header, 1 pin [form="♀ (female)"]
  J289 = female pin header, 1 pin [form="♀ (female)"]  # not connected
  J290 = female pin header, 1 pin [form="♀ (female)"]  # not connected
  J291 = female pin header, 1 pin [form="♀ (female)"]  # not connected
  J292 = female pin header, 1 pin [form="♀ (female)"]  # not connected
  J293 = female pin header, 1 pin [form="♀ (female)"]
  J294 = female pin header, 1 pin [form="♀ (female)"]
  J295 = female pin header, 1 pin [form="♀ (female)"]
  J296 = female pin header, 1 pin [form="♀ (female)"]
  J297 = female pin header, 1 pin [form="♀ (female)"]  # not connected
  J287 = male pin header, 1 pin [form="♂ (male)"]
  J298 = female pin header, 1 pin [form="♀ (female)"]  # not connected
  J287_2 = female pin header, 1 pin [form="♀ (female)"]
  J299 = female pin header, 1 pin [form="♀ (female)"]  # not connected
  J300 = female pin header, 1 pin [form="♀ (female)"]  # not connected
  J301 = female pin header, 1 pin [form="♀ (female)"]
  J302 = female pin header, 1 pin [form="♀ (female)"]  # not connected

nets:
  N1: IC1.A_!A!_B, J2.pin1
  N2: IC1.A_1A, J2.pin2
  N3: IC1.A_1B, J2.pin3
  N4: IC1.A_1Y, J2.pin4
  N5: IC1.A_2A, J2.pin5
  N6: IC1.A_2B, J2.pin6
  N7: IC1.A_2Y, J2.pin7
  N8: IC1.P_GND, J2.pin8
  N9: IC1.A_3Y, J1.pin8
  N10: IC1.A_3B, J1.pin7
  N11: IC1.A_3A, J1.pin6
  N12: IC1.A_4Y, J1.pin5
  N13: IC1.A_4B, J1.pin4
  N14: IC1.A_4A, J1.pin3
  N15: IC1.A_G, J1.pin2
  N16: IC1.P_VCC, J1.pin1
  N17: IC2.A_!A!_B, J3.pin1
  N18: IC2.A_1A, J3.pin2
  N19: IC2.A_1B, J3.pin3
  N20: IC2.A_1Y, J3.pin4
  N21: IC2.A_2A, J3.pin5
  N22: IC2.A_2B, J3.pin6
  N23: IC2.A_2Y, J3.pin7
  N24: IC2.P_GND, J3.pin8
  N25: IC2.A_3Y, J4.pin8
  N26: IC2.A_3B, J4.pin7
  N27: IC2.A_3A, J4.pin6
  N28: IC2.A_4Y, J4.pin5
  N29: IC2.A_4B, J4.pin4
  N30: IC2.A_4A, J4.pin3
  N31: IC2.A_G, J4.pin2
  N32: IC2.P_VCC, J4.pin1
  N33: IC3.A_!A!_B, J5.pin1
  N34: IC3.A_1A, J5.pin2
  N35: IC3.A_1B, J5.pin3
  N36: IC3.A_1Y, J5.pin4
  N37: IC3.A_2A, J5.pin5
  N38: IC3.A_2B, J5.pin6
  N39: IC3.A_2Y, J5.pin7
  N40: IC3.P_GND, J5.pin8
  N41: IC3.A_3Y, J6.pin8
  N42: IC3.A_3B, J6.pin7
  N43: IC3.A_3A, J6.pin6
  N44: IC3.A_4Y, J6.pin5
  N45: IC3.A_4B, J6.pin4
  N46: IC3.A_4A, J6.pin3
  N47: IC3.A_G, J6.pin2
  N48: IC3.P_VCC, J6.pin1
  N49: R1.Pin_1, R2.Pin_0, J7.pin1, J7.pin2
  N50: R2.Pin_1, R3.Pin_0, J8.pin1, J8.pin2
  N51: R3.Pin_1, R4.Pin_0, J9.pin1, J9.pin2
  N52: R4.Pin_1, R5.Pin_0, J10.pin1, J10.pin2
  N53: R5.Pin_1, J11.pin1
  N54: R6.Pin_0, J11.pin2
  N55: R6.Pin_1, R7.Pin_0, J14.pin1, J14.pin2
  N56: R7.Pin_1, R8.Pin_0, J15.pin1, J15.pin2
  N57: R8.Pin_1, R9.Pin_0, J13.pin1, J13.pin2
  N58: R9.Pin_1, R10.Pin_0, J12.pin1, J12.pin2
  N59: R10.Pin_1, R20.Pin_0, J16.pin1, J16.pin2
  N60: R11.Pin_0, R20.Pin_1, J19.pin1, J19.pin2
  N61: R11.Pin_1, R19.Pin_0, J20.pin1, J20.pin2
  N62: R12.Pin_0, R18.Pin_1, J25.pin1, J25.pin2
  N63: R12.Pin_1, R15.Pin_0, J23.pin1, J23.pin2
  N64: R13.Pin_0, R17.Pin_1, J17.pin1, J17.pin2
  N65: R13.Pin_1, R16.Pin_0, J21.pin1, J21.pin2
  N66: R14.Pin_0, R15.Pin_1, J22.pin1, J22.pin2
  N67: R14.Pin_1, R21.Pin_0, J26.pin1, J26.pin2
  N68: R16.Pin_1, R18.Pin_0, J24.pin1, J24.pin2
  N69: R17.Pin_0, R19.Pin_1, J18.pin1, J18.pin2
  N70: R22.Pin_0, J37.pin2
  N71: R23.Pin_0, J44.pin2
  N72: R23.Pin_1, J55.pin1
  N73: R24.Pin_0, J42.pin1, J42.pin2
  N74: R24.Pin_1, J48.pin1, J48.pin2
  N75: R25.Pin_0, J49.pin2
  N76: R25.Pin_1, J45.pin1
  N77: R26.Pin_0, J41.pin2
  N78: R26.Pin_1, J46.pin1
  N79: R27.Pin_0, J51.pin2
  N80: R27.Pin_1, J50.pin1
  N81: R28.Pin_0, J45.pin2
  N82: R28.Pin_1, J39.pin1
  N83: R29.Pin_1, J38.pin1
  N84: R30.Pin_0, J47.pin2
  N85: R30.Pin_1, J37.pin1
  N86: R31.Pin_0, J40.pin2
  N87: R31.Pin_1, J53.pin1
  N88: R32.Pin_0, J43.pin2
  N89: R32.Pin_1, J52.pin1
  N90: R33.Pin_0, J36.pin2
  N91: R33.Pin_1, J49.pin1
  N92: R34.Pin_0, J55.pin2
  N93: R34.Pin_1, J43.pin1
  N94: R35.Pin_0, J52.pin2
  N95: R36.Pin_0, J53.pin2
  N96: R36.Pin_1, J44.pin1
  N97: R37.Pin_0, J54.pin2
  N98: R37.Pin_1, J41.pin1
  N99: R38.Pin_1, J36.pin1
  N100: R39.Pin_0, J50.pin2
  N101: R39.Pin_1, J40.pin1
  N102: R40.Pin_0, J39.pin2
  N103: R40.Pin_1, J54.pin1
  N104: R41.Pin_0, J46.pin2
  N105: R41.Pin_1, J47.pin1
  N106: R42.Pin_0, J38.pin2
  N107: R42.Pin_1, J51.pin1
  N108: IC4.A_!A!_B, IC4.P_VCC, J27.pin1, J28.pin1
  N109: IC4.A_1A, IC4.A_G, J27.pin2, J28.pin2
  N110: IC4.A_1B, IC4.A_4A, J27.pin3, J28.pin3
  N111: IC4.A_1Y, IC4.A_4B, J27.pin4, J28.pin4
  N112: IC4.A_2A, IC4.A_4Y, J27.pin5, J28.pin5
  N113: IC4.A_2B, IC4.A_3A, J27.pin6, J28.pin6
  N114: IC4.A_2Y, IC4.A_3B, J27.pin7, J28.pin7
  N115: IC4.P_GND, IC4.A_3Y, J27.pin8, J28.pin8
  N116: IC5.A_!A!_B, IC5.P_VCC, J29.pin1, J30.pin1
  N117: IC5.A_1A, IC5.A_G, J29.pin2, J30.pin2
  N118: IC5.A_1B, IC5.A_4A, J29.pin3, J30.pin3
  N119: IC5.A_1Y, IC5.A_4B, J29.pin4, J30.pin4
  N120: IC5.A_2A, IC5.A_4Y, J29.pin5, J30.pin5
  N121: IC5.A_2B, IC5.A_3A, J29.pin6, J30.pin6
  N122: IC5.A_2Y, IC5.A_3B, J29.pin7, J30.pin7
  N123: IC5.P_GND, IC5.A_3Y, J29.pin8, J30.pin8
  N124: IC6.A_!A!_B, IC6.P_VCC, J31.pin1, J32.pin1
  N125: IC6.A_1A, IC6.A_G, J31.pin2, J32.pin2
  N126: IC6.A_1B, IC6.A_4A, J31.pin3, J32.pin3
  N127: IC6.A_1Y, IC6.A_4B, J31.pin4, J32.pin4
  N128: IC6.A_2A, IC6.A_4Y, J31.pin5, J32.pin5
  N129: IC6.A_2B, IC6.A_3A, J31.pin6, J32.pin6
  N130: IC6.A_2Y, IC6.A_3B, J31.pin7, J32.pin7
  N131: IC6.P_GND, IC6.A_3Y, J31.pin8, J32.pin8
  N132: J174.pin1, J180.pin1, J182.pin1, J183.pin1, J184.pin1, J185.pin1, J188.pin1, J189.pin1, J191.pin1, J194.pin1, J196.pin1, J197.pin1, J198.pin1, J199.pin1, J200.pin1, J201.pin1, R67.Pin_0, R67.Pin_1, R68.Pin_0, R68.Pin_1, R69.Pin_0, R69.Pin_1, R70.Pin_0, R70.Pin_1, R73.Pin_0, R73.Pin_1, R74.Pin_0, R74.Pin_1, R75.Pin_0, R75.Pin_1, R76.Pin_0, R76.Pin_1, R77.Pin_0, R77.Pin_1, R78.Pin_0, R78.Pin_1, R79.Pin_0, R79.Pin_1, R80.Pin_0, R80.Pin_1, R81.Pin_0, R81.Pin_1, R82.Pin_0, R82.Pin_1, R83.Pin_0, R83.Pin_1, R84.Pin_0, R84.Pin_1, R85.Pin_0, R85.Pin_1, R86.Pin_0, R86.Pin_1, J204.pin1, J205.pin1, R87.Pin_0, R87.Pin_1, R88.Pin_0, R88.Pin_1, J206.pin1, J207.pin1, R89.Pin_0, R89.Pin_1
  N133: R90.Pin_0, R90.Pin_1
  N134: R91.Pin_0, R91.Pin_1
  N135: R92.Pin_0, R92.Pin_1
  N136: R93.Pin_0, R93.Pin_1
  N137: R94.Pin_0, R94.Pin_1
  N138: R95.Pin_0, R95.Pin_1
  N139: R96.Pin_0, R96.Pin_1
  N140: R97.Pin_0, R97.Pin_1
  N141: R98.Pin_0, R98.Pin_1
  N142: R99.Pin_0, R99.Pin_1
  N143: R100.Pin_0, R100.Pin_1
  N144: R101.Pin_0, R101.Pin_1
  N145: R102.Pin_0, R102.Pin_1
  N146: R103.Pin_0, R103.Pin_1
  N147: R104.Pin_0, R104.Pin_1
  N148: R105.Pin_0, R105.Pin_1
  N149: R106.Pin_0, R106.Pin_1
  N150: R107.Pin_0, R107.Pin_1
  N151: R108.Pin_0, R108.Pin_1
  N152: R109.Pin_0, R109.Pin_1
  N153: R110.Pin_0, R110.Pin_1
  N154: J228.pin4, J262.pin1
  N155: J228.pin5, J263.pin1
  N156: J228.pin7, J264.pin1
  N157: J228.pin8, J265.pin1
  N158: J229.pin4, J261.pin1
  N159: J229.pin5, J258.pin1
  N160: J229.pin6, J259.pin1
  N161: J229.pin7, J260.pin1
  N162: J229.pin8, J301.pin1
  N163: J231.pin4, J295.pin1
  N164: J231.pin5, J285.pin1
  N165: J231.pin7, J296.pin1
  N166: J231.pin8, J293.pin1
  N167: J232.pin4, J294.pin1
  N168: J232.pin5, J288.pin1
  N169: J232.pin6, J284.pin1
  N170: J232.pin7, J286.pin1
  N171: J235.pin4, J270.pin1
  N172: J235.pin5, J267.pin1
  N173: J235.pin7, J271.pin1
  N174: J235.pin8, J266.pin1
  N175: J236.pin4, J269.pin1
  N176: J236.pin5, J272.pin1
  N177: J236.pin6, J268.pin1
  N178: J236.pin7, J273.pin1
  N179: J243.pin4, J276.pin1
  N180: J243.pin5, J275.pin1
  N181: J243.pin6, J277.pin1
  N182: J243.pin7, J274.pin1
  N183: J287.pin1, J287_2.pin1
